# Fritzing sketch projeto (saved by Fritzing 0.8.7b)
breadboards: 1

parts:
  U1 = ESP8266 NodeMCU LoLin module
  Componente1 = Logic Level Converter
  KY-1 = Keyes Relay [package=THT]
  M1 = DC Motor
  VCC1 = Battery

nets:
  GND: U1.GND, Componente1.GND, KY-1.ground
  N1: U1.D5, Componente1.TX_LV
  N2: U1.Vin, Componente1.HV, KY-1.power
  N3: U1.3V3, Componente1.LV
  N4: Componente1.TX_HV, KY-1.signal
  N5: KY-1.NC, M1.pin_2
  N6: KY-1.C, VCC1.-

custom parts:
  ESP8266 NodeMCU LoLin module: ESP8266 based NodeMCU
  Keyes Relay: The Keyes 5V relay module is suitable for SCM development, home appliance control. It uses a 5V~12V TIL control signal which can control DC / AC signal.
